// Logisim project ALU_external_cin_logic.circ as structural Verilog: 1 circuit, main circuit main
module main (
  input  ROM_ALU_1,
  input  ROM_ALU_2,
  input  ROM_ALU_3,
  input  ROM_ALU_4,
  input  ROM_ALU_5,
  input  FLAG_C,
  output ALU_SEL_1,
  output ALU_SEL_2,
  output ALU_SEL_3,
  output ALU_SEL_4,
  output ALU_SEL_5
);

  wire nor_1_out, nor_2_out, nor_3_out;

  nor nor_1 (nor_1_out, ROM_ALU_1, ROM_ALU_2, ROM_ALU_2);
  nor nor_2 (nor_2_out, ROM_ALU_4, ROM_ALU_4, ROM_ALU_4);
  nor nor_3 (nor_3_out, ROM_ALU_5, nor_2_out, nor_1_out);
  Multiplexer #(.enable("false")) multiplexer_1 (.in0(ROM_ALU_2), .in1(FLAG_C), .out(ALU_SEL_2), .sel(nor_3_out));
  LED ALU_CIN_OVERRIDE (.in(nor_3_out));

  assign ALU_SEL_1 = ROM_ALU_1;
  assign ALU_SEL_3 = ROM_ALU_3;
  assign ALU_SEL_4 = ROM_ALU_4;
  assign ALU_SEL_5 = ROM_ALU_5;

  // Notes on the sheet:
  //   Lo bit
  //   ALU_CIN_OVERRIDE = a NOR NOT b NOR (d NOR e) 
  //   74HCT27 Triple 3 input NOR
  //   1 bit multiplexer = (SEL NAND X) NAND (NOT SEL NAND Y) 
  //   If ALU_CIN_OVERRIDE is set then ALU_SEL_2 tracks FLAG_C, otherwise ALU_SEL_2 tracks ROM_ALU_2
  //   ??? Less space and wiring if use EEPROM : https://www.mouser.co.uk/ProductDetail/Greenliant/GLS29EE010-70-4C-PHE?qs=bAdOcXfFoy08hG5CPsLclg%3D%3D
  //   74HCT157 2:1 multiplexer
endmodule
