// Logisim project CPU21_PC_AS_COUNTING_REG.circ as structural Verilog: 3 circuits, main circuit main
module main (
);

  wire A_in, A_OUT, ALU_1, ALU_2, ALU_Carry_In, ALU_Carry_Out, ALU_EQ_OUT, ALU_out, ALU_ZERO_OUT, and_2_out,
       and_3_out, and_4_out, B_in, B_OUT, clk, ctl_clk, DISP_in, FLAG_Carry, FLAG_Eq, FLAG_Z, MAR_in,
       MAR_out, not_1_out, not_2_out, not_3_out, PC_in, PC_out, PCC_in, PCU_in, PCZ_in, RAM_in, RAM_out,
       RESET, ROM_out, s_r_ff_1_q, UNUSED;
  wire [5:0] OpCode;
  wire [7:0] ALUVal, AVal, BVal, Data_bus, DisplayVal, inst_count, MARVal, Operand, PCVal;

  Button button_1 (.out(RESET));
  LED led_1 (.in(clk));
  LED led_2 (.in(ctl_clk));
  // Probe on AVal
  // Probe on BVal
  LED led_3 (.in(ALU_Carry_In));
  // Probe on PCVal
  // Probe on MARVal
  LED led_4 (.in(FLAG_Carry));
  LED led_5 (.in(FLAG_Eq));
  LED led_6 (.in(FLAG_Z));
  LED led_7 (.in(DISP_in));
  LED led_8 (.in(A_in));
  LED led_9 (.in(B_in));
  LED led_10 (.in(MAR_in));
  LED led_11 (.in(RAM_in));
  LED led_12 (.in(PC_in));
  LED led_13 (.in(1'b0));
  LED led_14 (.in(PCC_in));
  // Probe on Data_bus
  // Probe on Data_bus
  Clock sysclk ();  // open: out
  // Probe on inst_count
  // Probe on DisplayVal
  // Probe on DisplayVal
  LED led_15 (.in(ALU_Carry_Out));
  LED led_16 (.in(ALU_EQ_OUT));
  LED led_17 (.in(ALU_ZERO_OUT));
  Register A_register (.D(Data_bus), .en(A_in), .clk(clk), .Q(AVal), .clr(RESET));
  Register B_register (.D(Data_bus), .en(B_in), .clk(clk), .Q(BVal), .clr(RESET));
  // Probe on ALUVal
  // Probe on {ALU_2, ALU_1, OpCode}
  // Probe on Operand
  // Probe on Data_bus
  LED led_18 (.in(PC_out));
  LED led_19 (.in(RAM_out));
  LED led_20 (.in(ROM_out));
  LED led_21 (.in(ALU_out));
  LED led_22 (.in(MAR_out));
  // Probe on ALU_1
  // Probe on ALU_2
  // Probe on AVal
  assign Data_bus = A_OUT ? AVal : 8'bz;  // Controlled_Buffer controlled_buffer_1
  assign Data_bus = B_OUT ? BVal : 8'bz;  // Controlled_Buffer controlled_buffer_2
  // Probe on BVal
  // Probe on Data_bus
  ROM PROGRAM_HIGH (.addr(PCVal), .data({ALU_2, ALU_1, OpCode}));
  // Probe on PCVal
  and and_1 (ALU_Carry_In, ALU_2, FLAG_Carry);
  // Probe on Data_bus
  // Probe on OpCode[2:0]
  // Probe on OpCode[5:3]
  Register MAR (.D(Data_bus), .en(MAR_in), .clk(clk), .Q(MARVal), .clr(RESET));
  Decoder #(.select(3), .enable("false")) decoder_1 (
    .out0(DISP_in), .out1(A_in), .out2(B_in), .out3(MAR_in), .out4(RAM_in), .out5(PCU_in), .out6(PCZ_in),
    .out7(PCC_in), .sel(OpCode[2:0]));
  Decoder #(.select(3), .enable("false")) decoder_2 (
    .out0(A_OUT), .out1(PC_out), .out2(RAM_out), .out3(ROM_out), .out4(ALU_out), .out5(MAR_out),
    .out6(B_OUT), .out7(UNUSED), .sel(OpCode[5:3]));
  // Probe on {ALU_2, ALU_1, OpCode}
  RAM #(.trigger("high")) ram_1 (.addr(MARVal), .we(RAM_in), .oe(RAM_out), .data(Data_bus));
  ROM PROGRAM_LOW (.addr(PCVal), .data(Operand));
  and and_2 (and_2_out, 1'b0, FLAG_Eq);
  and and_3 (and_3_out, PCC_in, FLAG_Carry);
  and and_4 (and_4_out, PCZ_in, FLAG_Z);
  // Probe on Operand
  or or_1 (PC_in, PCU_in, and_2_out, and_3_out, and_4_out);
  Pull_Resistor pull_resistor_1 (.node(Data_bus[0]));
  Pull_Resistor pull_resistor_2 (.node(Data_bus[1]));
  Pull_Resistor pull_resistor_3 (.node(Data_bus[2]));
  Pull_Resistor pull_resistor_4 (.node(Data_bus[3]));
  Pull_Resistor pull_resistor_5 (.node(Data_bus[4]));
  Pull_Resistor pull_resistor_6 (.node(Data_bus[5]));
  Pull_Resistor pull_resistor_7 (.node(Data_bus[6]));
  Pull_Resistor pull_resistor_8 (.node(Data_bus[7]));
  assign Data_bus = ROM_out ? Operand : 8'bz;  // Controlled_Buffer controlled_buffer_3
  S_R_Flip_Flop s_r_ff_1 (.S(1'b0), .R(1'b1), .clk(ctl_clk), .Q(s_r_ff_1_q), .preset(RESET));  // open: reset, Qn
  Register DISP_register (.D(Data_bus), .en(DISP_in), .clk(clk), .Q(DisplayVal), .clr(RESET));
  Counter counter_1 (
    .clr(s_r_ff_1_q), .load(PC_in), .up(1'b1), .count(1'b1), .clk(ctl_clk), .D(Data_bus), .Q(PCVal));  // open: carry
  // Probe on Data_bus
  PlusMinus4BitUsing4Bit plusminus4bitusing4bit_1 (
    .C(ALU_Carry_Out), .F(ALUVal), .subtract(ALU_1), .cin(ALU_Carry_In), .Z(ALU_ZERO_OUT), .y(BVal),
    .x(AVal), .EQ(ALU_EQ_OUT));  // open: GT, N, LT
  Register #(.width(3)) FLAG_register (
    .D({ALU_ZERO_OUT, ALU_EQ_OUT, ALU_Carry_Out}), .en(ALU_out), .clk(clk),
    .Q({FLAG_Z, FLAG_Eq, FLAG_Carry}), .clr(RESET));
  // Probe on DisplayVal
  // Probe on {FLAG_Z, FLAG_Eq, FLAG_Carry}
  assign Data_bus = ALU_out ? ALUVal : 8'bz;  // Controlled_Buffer controlled_buffer_4
  // Probe on PCVal
  assign Data_bus = PC_out ? PCVal : 8'bz;  // Controlled_Buffer controlled_buffer_5
  Clock clock_1 (.out(ctl_clk));
  // Probe on A_OUT
  // Probe on B_OUT
  // Probe on PC_out
  // Probe on RAM_out
  // Probe on ROM_out
  // Probe on ALU_out
  // Probe on MAR_out
  // Probe on {ALU_2, ALU_1, OpCode}
  // Probe on Operand
  // Probe on AVal
  // Probe on BVal
  // Probe on FLAG_Carry
  // Probe on FLAG_Eq
  // Probe on FLAG_Z
  // Probe on ALU_1
  // Probe on ALUVal
  // Probe on PCVal
  not not_1 (not_1_out, PC_in);
  // Probe on not_1_out
  // Probe on A_in
  // Probe on B_in
  not not_2 (not_2_out, ctl_clk);
  not not_3 (not_3_out, not_2_out);
  // Probe on Data_bus
  // Probe on clk
  LED led_23 (.in(clk));
  not not_4 (clk, not_3_out);
  LED led_24 (.in(ctl_clk));
  // Probe on ctl_clk
  Counter #(.ongoal("stay")) counter_2 (
    .clr(RESET), .load(1'b0), .up(1'b1), .count(1'b1), .clk(clk), .Q(inst_count));  // open: D, carry

  // Other names for the same wires on the sheet: RawClock = ctl_clk; FLAGS_val[2:0] = {FLAG_Z, FLAG_Eq, FLAG_Carry};
  //   OpCode[7:6] = {ALU_2, ALU_1}; ResetButton = RESET

  // Notes on the sheet:
  //   Front Panel
  //   General Purpose Registers
  //   RAM
  //   contents of PROGRAM_HIGH (hex, n*v repeats v):
  //   18 19 1a 21 1f 1d 18 1d 18 1d 19 1a 21 1e 1d 18 1d 18 1d 19 1a 61 1e 1d 18 1d 18 1d 19 1a 61 1f 1d
  //   18 1d 18 1d 1d 1f 1d 18 1d 18 1d
  //   Program ROMs
  //   Decoder Logic
  //   PCE_IN NOT YET IMPL
  //   contents of PROGRAM_LOW (hex, n*v repeats v):
  //   0 ff 1 0 6 8 1 a e1 9 ff 1 0 f 11 2 13 e2 12 ff ff 0 18 1a 3 1c e3 1b 1 2 0 21 23 4 25 e4 24 25 28
  //   2a 4 21 e4 2b
  //   CMOS BUS must always never be left floating - Safety measure incase of fault
  //   8 Bit ALU
  //   Flags Register
  //   Display Register
  //   Program Counter
  //   SR needed to hold reset high until clock
  //   Probe Points
  //   Clock Splitter
  //   Ben Eater - invert the main clock to delay it slightly so that the control lines change first
  //   Instruction Counter
endmodule

module PlusMinus4BitUsing4Bit (
  input  [7:0] x,
  input  [7:0] y,
  input  subtract,
  input  cin,
  output [7:0] F,
  output Z,
  output C,
  output N,
  output GT,
  output EQ,
  output LT
);

  wire adder_1_cout, adder_2_cout, comparator_1_lt, or_1_out;
  wire [7:0] xor_1_out;

  assign xor_1_out = y ^ {8{subtract}};  // XOR_Gate xor_1, 8 bits wide
  or or_1 (or_1_out, subtract, cin);
  Adder #(.width(4)) adder_1 (.a(x[3:0]), .b(xor_1_out[3:0]), .out(F[3:0]), .cin(or_1_out), .cout(adder_1_cout));
  Adder #(.width(4)) adder_2 (.a(x[7:4]), .b(xor_1_out[7:4]), .out(F[7:4]), .cin(adder_1_cout), .cout(adder_2_cout));
  xor xor_2 (C, adder_2_cout, subtract);
  and and_1 (N, C, subtract);
  Comparator comparator_1 (.a(x), .b(y), .gt(GT), .eq(EQ), .lt(comparator_1_lt));
  nor nor_1 (Z, F[0], F[1], F[2], F[3], F[4], F[5], F[6], F[7]);
  LED X_GT_Y (.in(GT));
  LED X_EQ_Y (.in(EQ));
  LED X_LT_Y (.in(comparator_1_lt));
  LED zero (.in(Z));

  assign LT = EQ;

  // Notes on the sheet:
  //   twos complement subtraction
  //   74ls283 4 bit adder
  //   74HC198/199 4 bit left right
  //   74HC595 shift register - serial in par out
  //   CD74HCT597E par in latched 
  //   cd74hc259 8 one bit addressable latches
  //   74hc299 par shift with i/o shared -  Shift Left, Shift Right, Load and Store - 3state
  //   74688 8 bit comparator does = and != only
  //   74682/684 8 bit comparator does = and < >         https://docs.isy.liu.se/pub/VanHeden/DataSheets/sn74ls682.pdf
  //   74hc323 par shift with i/o shared -  Shift Left, Shift Right, Load and Store 3 state
endmodule

module PRESETABLE_COUNTER (
);

  wire clk, RESET;
  wire [7:0] inst_count;

  Counter #(.ongoal("stay")) counter_1 (
    .clr(RESET), .load(1'b0), .up(1'b1), .count(1'b1), .clk(clk), .Q(inst_count));  // open: D, carry
endmodule
