// Logisim project LevelToPulseConverter.circ as structural Verilog: 1 circuit, main circuit main
module main (
  input  en,
  output pulsed
);

  wire clock_1_out, nand_1_out, nand_2_out, nand_3_out;

  Clock #(.highDuration(50), .lowDuration(50)) clock_1 (.out(clock_1_out));
  nand nand_1 (nand_1_out, clock_1_out, clock_1_out);
  // Probe on nothing
  Clock sysclk ();  // open: out
  nand nand_2 (nand_2_out, nand_1_out, en);
  // Probe on nand_2_out
  nand nand_3 (nand_3_out, nand_2_out, nand_2_out);
  nand nand_4 (pulsed, clock_1_out, nand_3_out);
  Counter counter_1 (.clr(1'b0), .load(1'b0), .up(1'b1), .count(1'b1), .clk(pulsed));  // open: D, carry, Q
endmodule
