// Logisim project OpenCollectorDemo.circ as structural Verilog: 2 circuits, main circuit OpenCollectorDemo
module OpenCollectorDemo (
  input  in_1,
  input  in_2,
  input  in_3,
  input  in_4
);

  wire controlled_buffer_1_out, controlled_buffer_2_out, not_1_out, not_2_out, not_3_out, opencollector_1_o,
       undriven;

  assign controlled_buffer_1_out = not_1_out ? undriven : 1'bz;  // Controlled_Buffer controlled_buffer_1
  not not_1 (not_1_out, undriven);
  OpenCollector opencollector_1 (.I(in_3), .O(opencollector_1_o));
  OpenCollector opencollector_2 (.I(in_4), .O(opencollector_1_o));
  // Probe on controlled_buffer_2_out
  assign controlled_buffer_2_out = not_2_out ? in_1 : 1'bz;  // Controlled_Buffer controlled_buffer_2
  not not_2 (not_2_out, in_1);
  assign controlled_buffer_2_out = not_3_out ? in_2 : 1'bz;  // Controlled_Buffer controlled_buffer_3
  not not_3 (not_3_out, in_2);
  // Probe on opencollector_1_o
  Pull_Resistor #(.pull(1)) pull_resistor_1 (.node(opencollector_1_o));
  // Probe on controlled_buffer_2_out
  Pull_Resistor #(.pull(1)) pull_resistor_2 (.node(controlled_buffer_2_out));

  // Notes on the sheet:
  //   0 or 1
  //   0 or X
  //   "open collector"
  //   "wired AND"
  //   74181 A=B is meant to be open collector so they can be wired together but this impl has them as ordinary logic
  //   we can wrap the library component to fix this
  //   0 or 1 if both are 1
endmodule

module OpenCollector (
  input  I,
  output O
);

  wire not_1_out;

  assign O = not_1_out ? I : 1'bz;  // Controlled_Buffer controlled_buffer_1
  not not_1 (not_1_out, I);
  // Probe on O
endmodule
