// Logisim project fred.circ as structural Verilog: 1 circuit, main circuit main
module main (
);

  wire [4:0] Opcode;
  wire [15:0] rom_1_data;

  DipSwitch #(.number(5)) dipswitch_1 (
    .sw1(Opcode[4]), .sw2(Opcode[3]), .sw3(Opcode[2]), .sw4(Opcode[1]), .sw5(Opcode[0]));
  // Probe on Opcode
  // Probe on {Opcode, {16{1'b0}}}
  ROM #(.addrWidth(21), .dataWidth(16)) rom_1 (.addr({Opcode, {16{1'b0}}}), .data(rom_1_data));
  // Probe on rom_1_data[15:12]
  // Probe on rom_1_data[11:8]
  Hex_Digit_Display hex_digit_display_1 (.value(rom_1_data[7:4]));  // open: dp
  Hex_Digit_Display hex_digit_display_2 (.value(rom_1_data[3:0]));  // open: dp

  // Notes on the sheet:
  //   switch 5 is carry in
  //   contents of rom_1 (hex, n*v repeats v):
  //   1122 3344 5566 7788 99aa bbcc ddee dead beef
  //   NZVC
  //   8-bit result
endmodule
